// Logisim project bcd.circ as structural Verilog: 12 circuits, main circuit main
module main (
);

  wire and_1_out, Checker_correct, clock_1_out, clock_2_out, clock_3_out, Not_Done, w0, w1, w2, w3;
  wire [3:0] counter_1_q;
  wire [6:0] Your_Answer;

  Inputs Inputs (.Clock(clock_1_out), .Not_Done(Not_Done), .w0(w0), .w1(w1), .w2(w2), .w3(w3));
  Clock clock_1 (.out(clock_1_out));
  part3 part3_1 (
    .w3(w3), .w2(w2), .w1(w1), .w0(w0), .a(Your_Answer[6]), .b(Your_Answer[5]), .c(Your_Answer[4]),
    .d(Your_Answer[3]), .e(Your_Answer[2]), .f(Your_Answer[1]), .g(Your_Answer[0]));
  // Probe on Your_Answer
  Checker Checker (.w0(w0), .w1(w1), .w2(w2), .w3(w3), .Your_Answer(Your_Answer), .Correct(Checker_correct));
  Shift_Register #(.length(10)) shift_register_1 (
    .shift(Not_Done), .in(Checker_correct), .clk(clock_2_out));  // open: out, load, clr, d0, q0, d1, q1, d2, q2, d3, q3, d4, q4, d5, q5, d6, q6, d7, q7, d8, q8, d9, q9
  Clock clock_2 (.out(clock_2_out));
  and and_1 (and_1_out, Checker_correct, Not_Done);
  Clock clock_3 (.out(clock_3_out));
  Counter #(.width(4), .max('hf), .ongoal("stay")) counter_1 (
    .count(and_1_out), .Q(counter_1_q), .clk(clock_3_out));  // open: load, D, carry, clr
  // Probe on counter_1_q

  // Notes on the sheet:
  //   Put Your Answer In Here
  //   Test 10
  //   Test 0
endmodule

module part3 (
  input  w3,
  input  w2,
  input  w1,
  input  w0,
  output a,
  output b,
  output c,
  output d,
  output e,
  output f,
  output g
);

  wire nw0, nw1, nw2, nw3;

  not not_1 (nw3, w3);
  not not_2 (nw2, w2);
  not not_3 (nw1, w1);
  not not_4 (nw0, w0);
  A a_1 (.w3(w3), .w2(w2), .w1(w1), .w0(w0), .Correct(a));
  B b_1 (.w3(w3), .w2(w2), .w1(w1), .w0(w0), .Correct(b));
  C c_1 (.w3(w3), .w2(w2), .w1(w1), .w0(w0), .Correct(c));
  D d_1 (.w3(w3), .w2(w2), .w1(w1), .w0(w0), .Correct(d));
  E e_1 (.w3(w3), .w2(w2), .w1(w1), .w0(w0), .Correct(e));
  F f_1 (.w3(w3), .w2(w2), .w1(w1), .w0(w0), .Correct(f));
  G g_1 (.w3(w3), .w2(w2), .w1(w1), .w0(w0), .Correct(g));
endmodule

module Inputs (
  input  Clock,
  output Not_Done,
  output w0,
  output w1,
  output w2,
  output w3
);

  wire comparator_1_eq;

  Counter #(.width(4), .max('ha), .ongoal("stay")) counter_1 (
    .count(1'b1), .Q({w3, w2, w1, w0}), .clk(Clock));  // open: load, D, carry, clr
  Comparator #(.width(4)) comparator_1 (.a(4'b1010), .b({w3, w2, w1, w0}), .eq(comparator_1_eq));  // open: gt, lt
  not not_1 (Not_Done, comparator_1_eq);
endmodule

module Checker (
  input  w0,
  input  w1,
  input  w2,
  input  w3,
  input  [6:0] Your_Answer,
  output Correct
);

  wire [6:0] rom_1_data;

  ROM #(.addrWidth(4), .dataWidth(7)) rom_1 (.addr({w3, w2, w1, w0}), .data(rom_1_data));  // open: sel
  Comparator #(.width(7)) comparator_1 (.a(rom_1_data), .b(Your_Answer), .eq(Correct));  // open: gt, lt

  // Notes on the sheet:
  //   contents of rom_1 (hex, n*v repeats v):
  //   7e 30 6d 79 33 5b 5f 70 7f 7b
endmodule

module F (
  input  w3,
  input  w2,
  input  w1,
  input  w0,
  output Correct
);

  wire and_1_out, and_2_out, and_3_out, nw0, nw1, nw2, nw3;

  not not_1 (nw3, w3);
  not not_2 (nw2, w2);
  not not_3 (nw1, w1);
  not not_4 (nw0, w0);
  and and_1 (and_1_out, nw1, nw0);
  and and_2 (and_2_out, w2, nw1);
  and and_3 (and_3_out, w2, nw0);
  or or_1 (Correct, w3, and_1_out, and_2_out, and_3_out);
endmodule

module A (
  input  w3,
  input  w2,
  input  w1,
  input  w0,
  output Correct
);

  wire and_1_out, and_2_out, nw0, nw1, nw2, nw3;

  not not_1 (nw3, w3);
  not not_2 (nw2, w2);
  not not_3 (nw1, w1);
  not not_4 (nw0, w0);
  and and_1 (and_1_out, w2, w0);
  and and_2 (and_2_out, nw2, nw0);
  or or_1 (Correct, and_1_out, w3, w1, and_2_out);
endmodule

module B (
  input  w3,
  input  w2,
  input  w1,
  input  w0,
  output Correct
);

  wire and_1_out, and_2_out, nw0, nw1, nw2, nw3;

  not not_1 (nw3, w3);
  not not_2 (nw2, w2);
  not not_3 (nw1, w1);
  not not_4 (nw0, w0);
  and and_1 (and_1_out, nw1, nw0);
  or or_1 (Correct, and_1_out, nw2, and_2_out);
  and and_2 (and_2_out, w1, w0);
endmodule

module C (
  input  w3,
  input  w2,
  input  w1,
  input  w0,
  output Correct
);

  wire nw0, nw1, nw2, nw3;

  not not_1 (nw3, w3);
  not not_2 (nw2, w2);
  not not_3 (nw1, w1);
  not not_4 (nw0, w0);
  or or_1 (Correct, nw1, w0, w2);
endmodule

module D (
  input  w3,
  input  w2,
  input  w1,
  input  w0,
  output Correct
);

  wire and_1_out, and_2_out, and_3_out, and_4_out, nw0, nw1, nw2, nw3;

  not not_1 (nw3, w3);
  not not_2 (nw2, w2);
  not not_3 (nw1, w1);
  not not_4 (nw0, w0);
  and and_1 (and_1_out, nw3, nw2, w1);
  and and_2 (and_2_out, nw2, nw0);
  and and_3 (and_3_out, w1, nw0);
  and and_4 (and_4_out, w2, nw1, w0);
  or or_1 (Correct, and_1_out, and_2_out, w3, and_3_out, and_4_out);
endmodule

module E (
  input  w3,
  input  w2,
  input  w1,
  input  w0,
  output Correct
);

  wire and_1_out, and_2_out, nw0, nw1, nw2, nw3;

  not not_1 (nw3, w3);
  not not_2 (nw2, w2);
  not not_3 (nw1, w1);
  not not_4 (nw0, w0);
  and and_1 (and_1_out, nw2, nw0);
  and and_2 (and_2_out, w1, nw0);
  or or_1 (Correct, and_1_out, and_2_out);
endmodule

module G (
  input  w3,
  input  w2,
  input  w1,
  input  w0,
  output Correct
);

  wire and_1_out, nw0, nw1, nw2, nw3, xor_1_axorb;

  not not_1 (nw3, w3);
  not not_2 (nw2, w2);
  not not_3 (nw1, w1);
  not not_4 (nw0, w0);
  XOR xor_1 (.A(w1), .B(w2), .AXORB(xor_1_axorb));
  and and_1 (and_1_out, w1, nw0);
  or or_1 (Correct, xor_1_axorb, w3, and_1_out);
endmodule

module XOR (
  input  A,
  input  B,
  output AXORB
);

  wire and_1_out, and_2_out, not_1_out, not_2_out;

  not not_1 (not_1_out, B);
  not not_2 (not_2_out, A);
  and and_1 (and_1_out, A, not_1_out);
  and and_2 (and_2_out, not_2_out, B);
  or or_1 (AXORB, and_1_out, and_2_out);
endmodule
