// Logisim project fun.circ as structural Verilog: 4 circuits, main circuit main
module main (
);

  wire and_1_out, Checker_correct, clock_1_out, clock_2_out, clock_3_out, NotDone, x1, x2, x3, x4, YourOut;
  wire [3:0] counter_1_q;

  Inputs Inputs (.Clock(clock_1_out), .NotDone(NotDone), .x4(x4), .x3(x3), .x2(x2), .x1(x1));
  Clock clock_1 (.out(clock_1_out));
  part1 part1_1 (.x4(x4), .x3(x3), .x2(x2), .x1(x1), .out(YourOut));
  Checker Checker (.x4(x4), .x3(x3), .x2(x2), .x1(x1), .YourSolution(YourOut), .Correct(Checker_correct));
  Shift_Register #(.length(16)) Correct (
    .shift(NotDone), .in(Checker_correct), .clk(clock_2_out));  // open: out, load, clr, d0, q0, d1, q1, d2, q2, d3, q3, d4, q4, d5, q5, d6, q6, d7, q7, d8, q8, d9, q9, d10, q10, d11, q11, d12, q12, d13, q13, d14, q14, d15, q15
  Clock clock_2 (.out(clock_2_out));
  and and_1 (and_1_out, Checker_correct, NotDone);
  Counter #(.width(4), .max('hf), .ongoal("stay")) counter_1 (
    .count(and_1_out), .Q(counter_1_q), .clk(clock_3_out));  // open: load, D, carry, clr
  Clock clock_3 (.out(clock_3_out));
  // Probe on counter_1_q

  // Notes on the sheet:
  //   Place your solution in here
  //   Number Correct
endmodule

module part1 (
  input  x4,
  input  x3,
  input  x2,
  input  x1,
  output out
);

  wire not_1_out, not_2_out, x1_x2_NOTx3_out, x1_x2_NOTx4_out, x3_x4_out;

  not not_1 (not_1_out, x4);
  not not_2 (not_2_out, x3);
  and x3_x4 (x3_x4_out, x4, x3);
  and x1_x2_NOTx4 (x1_x2_NOTx4_out, not_1_out, x2, x1);
  and x1_x2_NOTx3 (x1_x2_NOTx3_out, not_2_out, x2, x1);
  or or_1 (out, x3_x4_out, x1_x2_NOTx4_out, x1_x2_NOTx3_out);
endmodule

module Inputs (
  input  Clock,
  output NotDone,
  output x4,
  output x3,
  output x2,
  output x1
);

  wire [4:4] counter_1_q;

  Counter #(.width(5), .max('h10), .ongoal("stay")) counter_1 (
    .count(1'b1), .Q({counter_1_q[4], x4, x3, x2, x1}), .clk(Clock));  // open: load, D, carry, clr
  not not_1 (NotDone, counter_1_q[4]);
endmodule

module Checker (
  input  x4,
  input  x3,
  input  x2,
  input  x1,
  input  YourSolution,
  output Correct
);

  wire rom_1_data;

  ROM #(.addrWidth(4), .dataWidth(1)) rom_1 (.addr({x4, x3, x2, x1}), .data(rom_1_data));  // open: sel
  Comparator #(.width(1)) comparator_1 (.a(rom_1_data), .b(YourSolution), .eq(Correct));  // open: gt, lt

  // Notes on the sheet:
  //   contents of rom_1 (hex, n*v repeats v):
  //   0 0 0 1 0 0 0 1 0 0 0 5*1
endmodule
