// Logisim project UpDownCounter.circ as structural Verilog: 7 circuits, main circuit main
module main (
  input  Halt_Enable
);

  wire and_2_out, CLK, Correct, Count_Down, Count_Up, Done_Testing, Halt, not_1_out, not_2_out, not_3_out;
  wire [2:0] Solution, Your_Answer;
  wire [5:0] counter_1_q;

  not not_1 (not_1_out, Correct);
  Clock clock_1 (.out(CLK));
  and and_1 (Halt, Halt_Enable, not_1_out);
  Inputs inputs_1 (.Halt(Halt), .CLK(CLK), .Count_Up(Count_Up), .Count_Down(Count_Down), .Done_Testing(Done_Testing));
  // Probe on Count_Up
  // Probe on Count_Down
  // Probe on Your_Answer
  // Probe on Solution
  Up_Down_Counter up_down_counter_1 (.Count_Up(Count_Up), .Count_Down(Count_Down), .CLK(CLK), .Count(Your_Answer));
  not not_2 (not_2_out, Halt);
  not not_3 (not_3_out, Done_Testing);
  Counter #(.width(6), .max('h21), .ongoal("stay")) counter_1 (
    .count(and_2_out), .Q(counter_1_q), .clk(CLK));  // open: load, D, carry, clr
  and and_2 (and_2_out, Correct, not_2_out, not_3_out);
  Checker checker_1 (
    .Halt_Enable(Halt_Enable), .Count_Up(Count_Up), .Count_Donw(Count_Down), .Your_Answer(Your_Answer),
    .CLK(CLK), .Correct(Correct), .Solution(Solution));
  // Probe on counter_1_q

  // Notes on the sheet:
  //   Your Solution in Here
  //   Max of 33
endmodule

module Up_Down_Counter (
  input  Count_Up,
  input  Count_Down,
  input  CLK,
  output [2:0] Count
);

  wire lsb_1_x0, mb_1_x1, msb_1_x2;

  MSB msb_1 (.MSB(Count[2]), .MB(Count[1]), .LSB(Count[0]), .Up(Count_Up), .Down(Count_Down), .x2(msb_1_x2));
  MB mb_1 (.MSB(Count[2]), .MB(Count[1]), .LSB(Count[0]), .Up(Count_Up), .Down(Count_Down), .x1(mb_1_x1));
  LSB lsb_1 (.MSB(Count[2]), .MB(Count[1]), .LSB(Count[0]), .Up(Count_Up), .Down(Count_Down), .x0(lsb_1_x0));
  D_Flip_Flop d_ff_1 (.clk(CLK), .D(msb_1_x2), .Q(Count[2]));  // open: Qn, preset, en, reset
  D_Flip_Flop d_ff_2 (.clk(CLK), .D(mb_1_x1), .Q(Count[1]));  // open: Qn, preset, en, reset
  D_Flip_Flop d_ff_3 (.clk(CLK), .D(lsb_1_x0), .Q(Count[0]));  // open: Qn, preset, en, reset

  // Other names for the same wires on the sheet: x0 = Count[0]; x1 = Count[1]; x2 = Count[2]; Down = Count_Down;
  //   Up = Count_Up
endmodule

module Inputs (
  input  Halt,
  input  CLK,
  output Count_Up,
  output Count_Down,
  output Done_Testing
);

  wire not_1_out;
  wire [5:0] counter_1_q;

  not not_1 (not_1_out, Halt);
  Counter #(.width(6), .max('h21), .ongoal("stay")) counter_1 (
    .count(not_1_out), .Q(counter_1_q), .carry(Done_Testing), .clk(CLK));  // open: load, D, clr
  ROM #(.addrWidth(6), .dataWidth(2)) rom_1 (.addr(counter_1_q), .data({Count_Up, Count_Down}));  // open: sel

  // Notes on the sheet:
  //   contents of rom_1 (hex, n*v repeats v):
  //   0 2 0 2 0 2 0 2 0 2 0 2 0 2 0 2 0 1 0 1 0 1 0 1 0 1 0 1 0 1 0 1
endmodule

module Checker (
  input  Halt_Enable,
  input  Count_Up,
  input  Count_Donw,
  input  [2:0] Your_Answer,
  input  CLK,
  output Correct,
  output [2:0] Solution
);

  wire and_1_out, and_2_out, and_3_out, Gate, nHalt_Enable, or_2_out;

  not not_1 (nHalt_Enable, Halt_Enable);
  and and_1 (and_1_out, Correct, Halt_Enable);
  and and_2 (and_2_out, Count_Up, Gate);
  or or_1 (Gate, nHalt_Enable, and_1_out);
  and and_3 (and_3_out, Gate, Count_Donw);
  or or_2 (or_2_out, and_3_out, and_2_out);
  Counter #(.width(3), .max('h7), .ongoal("stay")) counter_1 (
    .load(and_3_out), .count(or_2_out), .Q(Solution), .clk(CLK));  // open: D, carry, clr
  Comparator #(.width(3)) comparator_1 (.a(Solution), .b(Your_Answer), .eq(Correct));  // open: gt, lt

  // Other names for the same wires on the sheet: Count_Down = Count_Donw
endmodule

module MSB (
  input  MSB,
  input  MB,
  input  LSB,
  input  Up,
  input  Down,
  output x2
);

  wire and_1_out, and_2_out, and_3_out, and_4_out, not_1_out;

  not not_1 (not_1_out, Down);
  and and_1 (and_1_out, MB, LSB, Up);
  and and_2 (and_2_out, MSB, not_1_out);
  and and_3 (and_3_out, MSB, LSB);
  and and_4 (and_4_out, MSB, MB);
  or or_1 (x2, and_1_out, and_2_out, and_3_out, and_4_out);
endmodule

module MB (
  input  MSB,
  input  MB,
  input  LSB,
  input  Up,
  input  Down,
  output x1
);

  wire and_1_out, and_2_out, and_3_out, and_4_out, and_5_out, not_1_out, not_2_out, not_3_out, not_4_out,
       not_5_out, not_6_out;

  not not_1 (not_1_out, MB);
  not not_2 (not_2_out, LSB);
  not not_3 (not_3_out, Down);
  not not_4 (not_4_out, Up);
  not not_5 (not_5_out, MB);
  not not_6 (not_6_out, LSB);
  and and_1 (and_1_out, not_1_out, LSB, Up);
  and and_2 (and_2_out, MB, not_2_out, not_3_out);
  and and_3 (and_3_out, MB, LSB, not_4_out);
  and and_4 (and_4_out, MSB, not_5_out, not_6_out, Down);
  and and_5 (and_5_out, MSB, MB, LSB);
  or or_1 (x1, and_1_out, and_2_out, and_3_out, and_4_out, and_5_out);
endmodule

module LSB (
  input  MSB,
  input  MB,
  input  LSB,
  input  Up,
  input  Down,
  output x0
);

  wire and_1_out, and_2_out, and_3_out, and_4_out, and_5_out, not_1_out, not_2_out, not_3_out, not_4_out,
       not_5_out;

  not not_1 (not_1_out, LSB);
  not not_2 (not_2_out, Up);
  not not_3 (not_3_out, Down);
  not not_4 (not_4_out, LSB);
  not not_5 (not_5_out, LSB);
  and and_1 (and_1_out, not_1_out, Up);
  and and_2 (and_2_out, LSB, not_2_out, not_3_out);
  and and_3 (and_3_out, MB, not_4_out, Down);
  and and_4 (and_4_out, MSB, not_5_out, Down);
  and and_5 (and_5_out, MSB, MB, Up);
  or or_1 (x0, and_1_out, and_2_out, and_3_out, and_4_out, and_5_out);
endmodule
