// Logisim project Vending.circ as structural Verilog: 5 circuits, main circuit main
module main (
  input  Halt_Enable
);

  wire and_2_out, CLK, Correct, Dime, Done_Testing, Give_Dime, Give_Merch, Give_Nickel, Halt, Nickel,
       not_1_out, not_2_out, not_3_out, Quarter, Sol_Give_Dime, Sol_Give_Merch, Sol_Give_Nickel;
  wire [8:0] counter_1_q, TestNumber;

  Clock clock_1 (.out(CLK));
  not not_1 (not_1_out, Correct);
  and and_1 (Halt, Halt_Enable, not_1_out);
  Inputs inputs_1 (
    .Halt(Halt), .CLK(CLK), .Quarter(Quarter), .Dime(Dime), .Nickel(Nickel), .TestNumber(TestNumber),
    .Done_Testing(Done_Testing));
  // Probe on Quarter
  // Probe on Dime
  // Probe on Nickel
  Vending vending_1 (
    .Quarter(Quarter), .Dime(Dime), .Nickel(Nickel), .CLK(CLK), .Give_Merchandise(Give_Merch),
    .Give_Dime(Give_Dime), .Give_Nickel(Give_Nickel));
  // Probe on Correct
  // Probe on Give_Merch
  // Probe on Sol_Give_Merch
  // Probe on Give_Dime
  // Probe on Sol_Give_Dime
  // Probe on Give_Nickel
  // Probe on Sol_Give_Nickel
  not not_2 (not_2_out, Halt);
  Checker checker_1 (
    .Give_Merch(Give_Merch), .Give_Dime(Give_Dime), .Give_Nickel(Give_Nickel), .TestNumber(TestNumber),
    .Correct(Correct), .Sol_Give_Merch(Sol_Give_Merch), .Sol_Give_Dime(Sol_Give_Dime),
    .Sol_Give_Nickel(Sol_Give_Nickel));
  and and_2 (and_2_out, Correct, not_2_out, not_3_out);
  not not_3 (not_3_out, Done_Testing);
  Counter #(.width(9), .max('h162), .ongoal("stay")) counter_1 (
    .count(and_2_out), .Q(counter_1_q), .clk(CLK));  // open: load, D, carry, clr
  // Probe on counter_1_q

  // Notes on the sheet:
  //   Max 354
endmodule

module Vending (
  input  Quarter,
  input  Dime,
  input  Nickel,
  input  CLK,
  output Give_Merchandise,
  output Give_Dime,
  output Give_Nickel
);

  wire S0, S0P, S1, S1P, S2, S2P;

  NextState nextstate_1 (
    .S2(S2), .S1(S1), .S0(S0), .Q(Quarter), .D(Dime), .N(Nickel), .S2P(S2P), .S1P(S1P), .S0P(S0P),
    .M(Give_Merchandise), .D2(Give_Dime), .N2(Give_Nickel));
  Register #(.width(3)) register_1 (.D({S0P, S1P, S2P}), .Q({S0, S1, S2}), .clk(CLK));  // open: en, clr

  // Other names for the same wires on the sheet: GD = Give_Dime; GN = Give_Nickel; M = Give_Merchandise;
  //   Quater = Quarter
endmodule

module Inputs (
  input  Halt,
  input  CLK,
  output Quarter,
  output Dime,
  output Nickel,
  output [8:0] TestNumber,
  output Done_Testing
);

  wire not_1_out;

  not not_1 (not_1_out, Halt);
  Counter #(.width(9), .max('h162), .ongoal("stay")) counter_1 (
    .count(not_1_out), .Q(TestNumber), .carry(Done_Testing), .clk(CLK));  // open: load, D, clr
  ROM #(.addrWidth(9), .dataWidth(3)) rom_1 (.addr(TestNumber), .data({Quarter, Dime, Nickel}));  // open: sel

  // Notes on the sheet:
  //   contents of rom_1 (hex, n*v repeats v):
  //   1 0 1 0 1 0 1 0 1 0 1 0 1 0 1 0 1 0 1 0 1 0 2 0 1 0 1 0 1 0 1 0 1 0 4 0 1 0 1 0 1 0 1 0 2 0 1 0 1 0
  //   1 0 1 0 4 0 1 0 1 0 1 0 1 0 2 0 1 0 1 0 1 0 2 0 2 0 1 0 1 0 1 0 2 0 4 0 1 0 1 0 1 0 4 0 1 0 1 0 1 0
  //   1 0 2 0 1 0 1 0 1 0 2 0 2 0 1 0 1 0 1 0 2 0 4 0 1 0 1 0 2 0 2 0 1 0 1 0 2 0 4 0 1 0 1 0 4 0 1 0 1 0
  //   1 0 1 0 2 0 1 0 1 0 1 0 2 0 2 0 1 0 1 0 1 0 2 0 4 0 1 0 1 0 2 0 2 0 1 0 1 0 2 0 4 0 1 0 1 0 2 0 2 0
  //   1 0 2 0 2 0 2 0 1 0 2 0 2 0 4 0 1 0 2 0 4 0 1 0 4 0 1 0 1 0 1 0 1 0 2 0 1 0 1 0 1 0 2 0 2 0 1 0 1 0
  //   1 0 2 0 4 0 1 0 1 0 2 0 2 0 1 0 1 0 2 0 4 0 1 0 1 0 2 0 2 0 1 0 2 0 2 0 2 0 1 0 2 0 2 0 4 0 1 0 2 0
  //   4 0 1 0 1 0 2 0 2 0 1 0 2 0 2 0 2 0 1 0 2 0 2 0 4 0 2 0 2 0 2 0 2 0 2 0 4 0 2 0 4 0 1 0 4 0 2 0 4 0
  //   4 0 4
endmodule

module Checker (
  input  Give_Merch,
  input  Give_Dime,
  input  Give_Nickel,
  input  [8:0] TestNumber,
  output Correct,
  output Sol_Give_Merch,
  output Sol_Give_Dime,
  output Sol_Give_Nickel
);

  ROM #(.addrWidth(9), .dataWidth(3)) rom_1 (
    .addr(TestNumber), .data({Sol_Give_Merch, Sol_Give_Dime, Sol_Give_Nickel}));  // open: sel
  Comparator #(.width(3)) comparator_1 (
    .a({Sol_Give_Merch, Sol_Give_Dime, Sol_Give_Nickel}), .b({Give_Merch, Give_Dime, Give_Nickel}),
    .eq(Correct));  // open: gt, lt

  // Other names for the same wires on the sheet: Solution[2:0] = {Sol_Give_Merch, Sol_Give_Dime, Sol_Give_Nickel};
  //   Your_Answer[2:0] = {Give_Merch, Give_Dime, Give_Nickel}

  // Notes on the sheet:
  //   contents of rom_1 (hex, n*v repeats v):
  //   10*0 4 11*0 5 11*0 7 9*0 4 9*0 7 9*0 4 9*0 5 9*0 7 7*0 6 9*0 4 9*0 5 9*0 7 7*0 4 7*0 7 5*0 5 9*0 4
  //   9*0 5 9*0 7 7*0 4 7*0 7 7*0 4 7*0 5 7*0 7 5*0 6 0 0 0 4 9*0 4 9*0 5 9*0 7 7*0 4 7*0 7 7*0 4 7*0 5
  //   7*0 7 5*0 6 7*0 4 7*0 5 7*0 7 5*0 4 5*0 7 0 0 0 5 0 0 0 4 0 0 0 5 0 0 0 7
endmodule

module NextState (
  input  S2,
  input  S1,
  input  S0,
  input  Q,
  input  D,
  input  N,
  output S2P,
  output S1P,
  output S0P,
  output M,
  output D2,
  output N2
);

  wire and_1_out, and_2_out, and_3_out, and_4_out, and_5_out, and_6_out, and_7_out, and_8_out, and_9_out,
       and_10_out, and_11_out, and_12_out, and_13_out, and_14_out, and_15_out, and_16_out, and_17_out,
       and_18_out, and_19_out, and_20_out, and_21_out, and_22_out, and_23_out, not_1_out, not_2_out,
       not_3_out, not_4_out, not_5_out, not_6_out, not_7_out, not_8_out, not_9_out, not_10_out, not_11_out,
       not_12_out, not_13_out, not_14_out, not_15_out, not_16_out, not_17_out, not_18_out, not_19_out,
       not_20_out, not_21_out, not_22_out, not_23_out, not_24_out, not_25_out, not_26_out, not_27_out;

  not not_1 (not_1_out, S2);
  not not_2 (not_2_out, S1);
  not not_3 (not_3_out, S0);
  not not_4 (not_4_out, S0);
  not not_5 (not_5_out, Q);
  not not_6 (not_6_out, D);
  not not_7 (not_7_out, Q);
  not not_8 (not_8_out, D);
  not not_9 (not_9_out, N);
  not not_10 (not_10_out, S2);
  not not_11 (not_11_out, S1);
  not not_12 (not_12_out, S2);
  not not_13 (not_13_out, S1);
  not not_14 (not_14_out, Q);
  not not_15 (not_15_out, D);
  not not_16 (not_16_out, N);
  not not_17 (not_17_out, S0);
  not not_18 (not_18_out, S0);
  not not_19 (not_19_out, S2);
  not not_20 (not_20_out, S1);
  not not_21 (not_21_out, S0);
  not not_22 (not_22_out, D);
  not not_23 (not_23_out, Q);
  not not_24 (not_24_out, D);
  not not_25 (not_25_out, N);
  not not_26 (not_26_out, S2);
  and and_1 (and_1_out, S0, Q);
  and and_2 (and_2_out, S1, Q);
  and and_3 (and_3_out, S2, D);
  and and_4 (and_4_out, S2, Q);
  and and_5 (and_5_out, S2, S0, N);
  and and_6 (and_6_out, S1, S0, Q);
  and and_7 (and_7_out, S2, Q);
  not not_27 (not_27_out, S0);
  and and_8 (and_8_out, not_1_out, not_2_out, not_3_out, Q);
  and and_9 (and_9_out, S1, D);
  and and_10 (and_10_out, S1, S0, N);
  and and_11 (and_11_out, S2, not_4_out, not_5_out, not_6_out);
  and and_12 (and_12_out, S2, not_7_out, not_8_out, not_9_out);
  and and_13 (and_13_out, not_10_out, not_11_out, D);
  and and_14 (and_14_out, not_12_out, not_13_out, S0, N);
  and and_15 (and_15_out, S1, not_14_out, not_15_out, not_16_out);
  and and_16 (and_16_out, S1, not_17_out, N);
  and and_17 (and_17_out, not_18_out, N);
  and and_18 (and_18_out, not_19_out, not_20_out, not_21_out, Q, not_22_out);
  and and_19 (and_19_out, S0, not_23_out, not_24_out, not_25_out);
  and and_20 (and_20_out, not_26_out, S0, D);
  or or_1 (M, and_1_out, and_2_out, and_3_out, and_4_out, and_5_out);
  or or_2 (D2, and_6_out, and_7_out);
  and and_21 (and_21_out, S1, not_27_out, Q);
  and and_22 (and_22_out, S2, Q);
  and and_23 (and_23_out, S2, S0, D);
  or or_3 (S2P, and_8_out, and_9_out, and_10_out, and_11_out, and_12_out);
  or or_4 (S1P, and_13_out, and_14_out, and_15_out, and_16_out);
  or or_5 (S0P, and_17_out, and_18_out, and_19_out, and_20_out);
  or or_6 (N2, and_21_out, and_22_out, and_23_out);
endmodule
