// Logisim project CPU.circ as structural Verilog: 4 circuits, main circuit CPU
module CPU (
);

  wire CLK, Halt, not_1_out, R_I, Reg_Write;
  wire [3:0] A, A_DATA, ALU_Res, B, B_DATA, C, multiplexer_1_out, OpCode;
  wire [4:0] counter_1_q;
  wire [15:0] rom_1_data;

  Clock clock_1 (.out(CLK));
  Counter #(.width(5), .max('h1f)) counter_1 (
    .count(not_1_out), .Q(counter_1_q), .clk(CLK));  // open: load, D, carry, clr
  not not_1 (not_1_out, Halt);
  ALU ALU (.OpCode(OpCode), .A(A_DATA), .B(multiplexer_1_out), .ALU_Res(ALU_Res));
  Multiplexer #(.width(4), .enable("false")) multiplexer_1 (.in0(B_DATA), .in1(B), .out(multiplexer_1_out), .sel(R_I));
  ROM #(.addrWidth(5), .dataWidth(16)) rom_1 (.addr(counter_1_q), .data(rom_1_data));  // open: sel
  Decoder Decoder (
    .Instruction(rom_1_data), .A(A), .B(B), .C(C), .OpCode(OpCode), .Reg_Write(Reg_Write), .R_I(R_I),
    .Halt(Halt));
  Reg_File Reg_File (
    .A(A), .B(B), .C(C), .Data_In(ALU_Res), .Reg_Write(Reg_Write), .CLK(CLK), .A_DATA(A_DATA), .B_DATA(B_DATA));

  // Notes on the sheet:
  //   Instructions
  //   contents of rom_1 (hex, n*v repeats v):
  //   2003 2106 1005 3210 4301 5433 6520 763c 8720 986f b938 ca77 db13 ec62 fd85 e05
endmodule

module Reg_File (
  input  [3:0] A,
  input  [3:0] B,
  input  [3:0] C,
  input  [3:0] Data_In,
  input  Reg_Write,
  input  CLK,
  output [3:0] A_DATA,
  output [3:0] B_DATA
);

  wire Write_Reg0, Write_Reg1, Write_Reg2, Write_Reg3, Write_Reg4, Write_Reg5, Write_Reg6, Write_Reg7,
       Write_Reg8, Write_Reg9, Write_Reg10, Write_Reg11, Write_Reg12, Write_Reg13, Write_Reg14, Write_Reg15;
  wire [3:0] Reg0, Reg1, Reg2, Reg3, Reg4, Reg5, Reg6, Reg7, Reg8, Reg9, Reg10, Reg11, Reg12, Reg13, Reg14,
       Reg15;

  Demultiplexer #(.select(4), .enable("false")) demultiplexer_1 (
    .out0(Write_Reg0), .out1(Write_Reg1), .out2(Write_Reg2), .out3(Write_Reg3), .out4(Write_Reg4),
    .out5(Write_Reg5), .out6(Write_Reg6), .out7(Write_Reg7), .out8(Write_Reg8), .out9(Write_Reg9),
    .out10(Write_Reg10), .out11(Write_Reg11), .out12(Write_Reg12), .out13(Write_Reg13), .out14(Write_Reg14),
    .out15(Write_Reg15), .in(Reg_Write), .sel(C));
  // Probe on Reg0
  Register #(.width(4)) u_Reg0 (.D(Data_In), .en(Write_Reg0), .Q(Reg0), .clk(CLK));  // open: clr
  // Probe on Reg4
  Register #(.width(4)) u_Reg4 (.D(Data_In), .en(Write_Reg4), .Q(Reg4), .clk(CLK));  // open: clr
  // Probe on Reg8
  Register #(.width(4)) u_Reg8 (.D(Data_In), .en(Write_Reg8), .Q(Reg8), .clk(CLK));  // open: clr
  // Probe on Reg12
  Register #(.width(4)) u_Reg12 (.D(Data_In), .en(Write_Reg12), .Q(Reg12), .clk(CLK));  // open: clr
  // Probe on Reg1
  Register #(.width(4)) u_Reg1 (.D(Data_In), .en(Write_Reg1), .Q(Reg1), .clk(CLK));  // open: clr
  // Probe on Reg5
  Register #(.width(4)) u_Reg5 (.D(Data_In), .en(Write_Reg5), .Q(Reg5), .clk(CLK));  // open: clr
  // Probe on Reg9
  Register #(.width(4)) u_Reg9 (.D(Data_In), .en(Write_Reg9), .Q(Reg9), .clk(CLK));  // open: clr
  // Probe on Reg13
  Register #(.width(4)) u_Reg13 (.D(Data_In), .en(Write_Reg13), .Q(Reg13), .clk(CLK));  // open: clr
  Register #(.width(4)) u_Reg2 (.D(Data_In), .en(Write_Reg2), .Q(Reg2), .clk(CLK));  // open: clr
  Register #(.width(4)) u_Reg6 (.D(Data_In), .en(Write_Reg6), .Q(Reg6), .clk(CLK));  // open: clr
  Register #(.width(4)) u_Reg10 (.D(Data_In), .en(Write_Reg10), .Q(Reg10), .clk(CLK));  // open: clr
  Register #(.width(4)) u_Reg14 (.D(Data_In), .en(Write_Reg14), .Q(Reg14), .clk(CLK));  // open: clr
  // Probe on Reg2
  // Probe on Reg6
  // Probe on Reg10
  // Probe on Reg14
  // Probe on Reg3
  Register #(.width(4)) u_Reg3 (.D(Data_In), .en(Write_Reg3), .Q(Reg3), .clk(CLK));  // open: clr
  // Probe on Reg7
  Register #(.width(4)) u_Reg7 (.D(Data_In), .en(Write_Reg7), .Q(Reg7), .clk(CLK));  // open: clr
  // Probe on Reg11
  Register #(.width(4)) u_Reg11 (.D(Data_In), .en(Write_Reg11), .Q(Reg11), .clk(CLK));  // open: clr
  // Probe on Reg15
  Register #(.width(4)) u_Reg15 (.D(Data_In), .en(Write_Reg15), .Q(Reg15), .clk(CLK));  // open: clr
  Multiplexer #(.select(4), .width(4), .enable("false")) multiplexer_1 (
    .in0(Reg0), .in1(Reg1), .in2(Reg2), .in3(Reg3), .in4(Reg4), .in5(Reg5), .in6(Reg6), .in7(Reg7),
    .in8(Reg8), .in9(Reg9), .in10(Reg10), .in11(Reg11), .in12(Reg12), .in13(Reg13), .in14(Reg14),
    .in15(Reg15), .out(A_DATA), .sel(A));
  Multiplexer #(.select(4), .width(4), .enable("false")) multiplexer_2 (
    .in0(Reg0), .in1(Reg1), .in2(Reg2), .in3(Reg3), .in4(Reg4), .in5(Reg5), .in6(Reg6), .in7(Reg7),
    .in8(Reg8), .in9(Reg9), .in10(Reg10), .in11(Reg11), .in12(Reg12), .in13(Reg13), .in14(Reg14),
    .in15(Reg15), .out(B_DATA), .sel(B));
endmodule

module ALU (
  input  [3:0] OpCode,
  input  [3:0] A,
  input  [3:0] B,
  output [3:0] ALU_Res
);

  wire [3:0] Add, And, Neg, Not, Or, Sub, Xor;

  assign And = A & B;  // AND_Gate and_1, 4 bits wide
  assign Or = A | B;  // OR_Gate or_1, 4 bits wide
  assign Xor = A ^ B;  // XOR_Gate xor_1, 4 bits wide
  assign Not = ~A;  // NOT_Gate not_1, 4 bits wide
  Negator #(.width(4)) negator_1 (.in(A), .out(Neg));
  Adder #(.width(4)) adder_1 (.a(A), .b(B), .out(Add));  // open: cin, cout
  Subtractor #(.width(4)) subtractor_1 (.a(A), .b(B), .out(Sub));  // open: bin, bout
  Multiplexer #(.select(4), .width(4), .enable("false")) multiplexer_1 (
    .in2(B), .in3(A), .in4(And), .in5(And), .in6(Or), .in7(Or), .in8(Xor), .in9(Xor), .in10(Not), .in11(Neg),
    .in12(Add), .in13(Add), .in14(Sub), .in15(Sub), .out(ALU_Res), .sel(OpCode));  // open: in0, in1

  // Other names for the same wires on the sheet: Load[3:0] = B; Move[3:0] = A
endmodule

module Decoder (
  input  [15:0] Instruction,
  output [3:0] A,
  output [3:0] B,
  output [3:0] C,
  output [3:0] OpCode,
  output Reg_Write,
  output R_I,
  output Halt
);

  wire or_1_out;

  Comparator #(.width(4), .mode("unsigned")) comparator_1 (
    .a(Instruction[15:12]), .b(4'b0001), .gt(Reg_Write));  // open: eq, lt
  Multiplexer #(.select(4), .enable("false")) multiplexer_1 (
    .in0(1'b0), .in1(1'b0), .in2(1'b1), .in3(1'b0), .in4(1'b0), .in5(1'b1), .in6(1'b0), .in7(1'b1),
    .in8(1'b0), .in9(1'b1), .in10(1'b0), .in11(1'b0), .in12(1'b0), .in13(1'b1), .in14(1'b0), .in15(1'b1),
    .out(R_I), .sel(Instruction[15:12]));
  not not_1 (Halt, or_1_out);
  or or_1 (or_1_out, Instruction[12], Instruction[13], Instruction[14], Instruction[15]);

  assign A = Instruction[7:4];
  assign B = Instruction[3:0];
  assign C = Instruction[11:8];
  assign OpCode = Instruction[15:12];

  // Other names for the same wires on the sheet: B_Imm[3:0] = Instruction[3:0]
endmodule
